// Logisim project AC.circ as structural Verilog: 2 circuits, main circuit main
module main (
  input  in_1,
  input  [3:0] in_2,
  input  in_3,
  input  in_4,
  input  in_5,
  input  in_6
);

  wire n74181_1_p1, n74181_1_p4, n74181_1_p6, n74181_1_p8, n74181_1_p9, n74181_1_p10, n74181_1_p11,
       n74181_1_p12, n74181_2_p1, n74181_2_p4, n74181_2_p6, n74181_2_p8, n74181_2_p9, n74181_2_p10,
       n74181_2_p11, n74181_2_p12, n74245_1_pin1, n74245_1_pin2, n74245_1_pin3, n74245_1_pin4, n74245_1_pin5,
       n74245_1_pin6, n74245_1_pin7, n74245_1_pin8, n74245_1_pin9, n74245_1_pin11, n74245_1_pin12,
       n74245_1_pin13, n74245_1_pin14, n74245_1_pin15, n74245_1_pin16, n74245_1_pin17, n74245_1_pin18,
       n74245_3_pin1, not_1_out, not_2_out, not_3_out, not_4_out;
  wire [7:0] ram_1_dout;

  not not_1 (not_1_out, in_5);
  _74245 u_74245_1 (
    .pin1(n74245_1_pin1), .pin2(n74245_1_pin2), .pin3(n74245_1_pin3), .pin4(n74245_1_pin4),
    .pin5(n74245_1_pin5), .pin6(n74245_1_pin6), .pin7(n74245_1_pin7), .pin8(n74245_1_pin8),
    .pin9(n74245_1_pin9), .pin19(not_1_out), .pin18(n74245_1_pin18), .pin17(n74245_1_pin17),
    .pin16(n74245_1_pin16), .pin15(n74245_1_pin15), .pin14(n74245_1_pin14), .pin13(n74245_1_pin13),
    .pin12(n74245_1_pin12), .pin11(n74245_1_pin11));
  // _74181 74181_1: pin names not known; wires that end beside it: n74181_1_p1, n74245_1_pin3, n74245_1_pin2, n74181_1_p4, n74245_1_pin4, n74181_1_p6, n74245_1_pin5, n74181_1_p8, n74181_1_p9, n74181_1_p10, n74181_1_p11, n74181_1_p12
  c74173 c74173_1 (
    .D2(n74245_1_pin17), .D3(n74245_1_pin16), .D4(n74245_1_pin15), .D1(n74245_1_pin18), .Q2(n74245_1_pin3),
    .Q3(n74245_1_pin4), .Q4(n74245_1_pin5), .Q1(n74245_1_pin2));  // open: CLK, nG1, nG2, CLR, M, N
  c74173 c74173_2 (
    .D2(n74245_1_pin13), .D3(n74245_1_pin12), .D4(n74245_1_pin11), .D1(n74245_1_pin14), .Q2(n74245_1_pin7),
    .Q3(n74245_1_pin8), .Q4(n74245_1_pin9), .Q1(n74245_1_pin6));  // open: CLK, nG1, nG2, CLR, M, N
  // _74181 74181_2: pin names not known; wires that end beside it: n74181_2_p1, n74245_1_pin7, n74245_1_pin6, n74181_2_p4, n74245_1_pin8, n74181_2_p6, n74245_1_pin9, n74181_2_p8, n74181_2_p9, n74181_2_p10, n74181_2_p11, n74181_2_p12
  not not_2 (not_2_out, in_1);
  _74245 u_74245_2 (
    .pin2(n74245_1_pin18), .pin3(n74245_1_pin17), .pin4(n74245_1_pin16), .pin5(n74245_1_pin15),
    .pin6(n74245_1_pin14), .pin7(n74245_1_pin13), .pin8(n74245_1_pin12), .pin9(n74245_1_pin11),
    .pin19(not_2_out), .pin18(n74181_1_p9), .pin17(n74181_1_p10), .pin16(n74181_1_p11), .pin15(n74181_1_p12),
    .pin14(n74181_2_p9), .pin13(n74181_2_p10), .pin12(n74181_2_p11), .pin11(n74181_2_p12));  // open: pin1
  not not_3 (not_3_out, in_6);
  _74245 u_74245_3 (
    .pin1(n74245_3_pin1), .pin2(n74181_1_p1), .pin3(n74181_2_p4), .pin4(n74181_2_p6), .pin5(n74181_2_p8),
    .pin6(n74181_2_p1), .pin7(n74181_1_p4), .pin8(n74181_1_p6), .pin9(n74181_1_p8), .pin19(not_3_out),
    .pin18(n74245_1_pin18), .pin17(n74245_1_pin17), .pin16(n74245_1_pin16), .pin15(n74245_1_pin15),
    .pin14(n74245_1_pin14), .pin13(n74245_1_pin13), .pin12(n74245_1_pin12), .pin11(n74245_1_pin11));
  c74173 c74173_3 (
    .D2(n74245_1_pin17), .D3(n74245_1_pin16), .D4(n74245_1_pin15), .D1(n74245_1_pin18), .Q2(n74181_2_p4),
    .Q3(n74181_2_p6), .Q4(n74181_2_p8), .Q1(n74181_1_p1));  // open: CLK, nG1, nG2, CLR, M, N
  RAM #(.addrWidth(4)) ram_1 (.addr(in_2), .we(not_4_out), .oe(in_3), .clk(in_4), .dout(ram_1_dout));  // open: din
  not not_4 (not_4_out, in_3);
  c74173 c74173_4 (
    .D2(n74245_1_pin13), .D3(n74245_1_pin12), .D4(n74245_1_pin11), .D1(n74245_1_pin14), .Q2(n74181_1_p4),
    .Q3(n74181_1_p6), .Q4(n74181_1_p8), .Q1(n74181_2_p1));  // open: CLK, nG1, nG2, CLR, M, N
  // also tied to VCC on the sheet: {n74245_1_pin1, n74245_3_pin1}
endmodule

module c74173 (
  input  D1,
  input  D2,
  input  D3,
  input  D4,
  input  CLK,
  input  nG1,
  input  nG2,
  input  CLR,
  input  M,
  input  N,
  output Q1,
  output Q2,
  output Q3,
  output Q4
);

  wire and_1_out, and_2_out, and_3_out, and_4_out, d_ff_1_q, d_ff_2_q, d_ff_3_q, d_ff_4_q, nor_1_out,
       nor_2_out;

  and and_1 (and_1_out, CLK, nor_1_out);
  and and_2 (and_2_out, CLK, nor_1_out);
  and and_3 (and_3_out, CLK, nor_1_out);
  and and_4 (and_4_out, CLK, nor_1_out);
  nor nor_1 (nor_1_out, nG1, nG2);
  D_Flip_Flop d_ff_1 (.D(D1), .clk(and_1_out), .Q(d_ff_1_q), .reset(CLR));  // open: Qn, preset
  D_Flip_Flop d_ff_2 (.D(D2), .clk(and_2_out), .Q(d_ff_2_q), .reset(CLR));  // open: Qn, preset
  D_Flip_Flop d_ff_3 (.D(D3), .clk(and_3_out), .Q(d_ff_3_q), .reset(CLR));  // open: Qn, preset
  D_Flip_Flop d_ff_4 (.D(D4), .clk(and_4_out), .Q(d_ff_4_q), .reset(CLR));  // open: Qn, preset
  nor nor_2 (nor_2_out, M, N);
  assign Q1 = nor_2_out ? d_ff_1_q : 1'bz;  // Controlled_Buffer controlled_buffer_1
  assign Q2 = nor_2_out ? d_ff_2_q : 1'bz;  // Controlled_Buffer controlled_buffer_2
  assign Q3 = nor_2_out ? d_ff_3_q : 1'bz;  // Controlled_Buffer controlled_buffer_3
  assign Q4 = nor_2_out ? d_ff_4_q : 1'bz;  // Controlled_Buffer controlled_buffer_4
endmodule
