// Logisim project BC.circ as structural Verilog: 2 circuits, main circuit main
module main (
);

  wire pull_resistor_1_node, pull_resistor_2_node, pull_resistor_3_node, pull_resistor_4_node,
       pull_resistor_5_node, pull_resistor_6_node, pull_resistor_7_node, pull_resistor_8_node,
       pull_resistor_9_node, pull_resistor_10_node, pull_resistor_11_node, pull_resistor_12_node,
       pull_resistor_13_node, pull_resistor_14_node, pull_resistor_15_node, pull_resistor_16_node;

  CLK clk_1 ();  // open: CLOCK_IN, HALT, CLOCK_OUT
  LED led_1 (.in(pull_resistor_1_node));
  LED led_2 (.in(pull_resistor_1_node));
  LED led_3 (.in(pull_resistor_2_node));
  LED led_4 (.in(pull_resistor_2_node));
  Pull_Resistor pull_resistor_1 (.node(pull_resistor_1_node));
  Pull_Resistor pull_resistor_2 (.node(pull_resistor_2_node));
  LED led_5 (.in(pull_resistor_3_node));
  LED led_6 (.in(pull_resistor_3_node));
  LED led_7 (.in(pull_resistor_4_node));
  LED led_8 (.in(pull_resistor_4_node));
  LED led_9 (.in(pull_resistor_5_node));
  LED led_10 (.in(pull_resistor_5_node));
  LED led_11 (.in(pull_resistor_6_node));
  Pull_Resistor pull_resistor_3 (.node(pull_resistor_3_node));
  Pull_Resistor pull_resistor_4 (.node(pull_resistor_4_node));
  Pull_Resistor pull_resistor_5 (.node(pull_resistor_5_node));
  Pull_Resistor pull_resistor_6 (.node(pull_resistor_6_node));
  LED led_12 (.in(pull_resistor_7_node));
  LED led_13 (.in(pull_resistor_8_node));
  LED led_14 (.in(pull_resistor_8_node));
  LED led_15 (.in(pull_resistor_9_node));
  LED led_16 (.in(pull_resistor_9_node));
  LED led_17 (.in(pull_resistor_10_node));
  LED led_18 (.in(pull_resistor_10_node));
  Pull_Resistor pull_resistor_7 (.node(pull_resistor_7_node));
  Pull_Resistor pull_resistor_8 (.node(pull_resistor_8_node));
  Pull_Resistor pull_resistor_9 (.node(pull_resistor_9_node));
  Pull_Resistor pull_resistor_10 (.node(pull_resistor_10_node));
  LED led_19 (.in(pull_resistor_11_node));
  LED led_20 (.in(pull_resistor_11_node));
  LED led_21 (.in(pull_resistor_12_node));
  LED led_22 (.in(pull_resistor_12_node));
  LED led_23 (.in(pull_resistor_13_node));
  LED led_24 (.in(pull_resistor_13_node));
  LED led_25 (.in(pull_resistor_14_node));
  Pull_Resistor pull_resistor_11 (.node(pull_resistor_11_node));
  Pull_Resistor pull_resistor_12 (.node(pull_resistor_12_node));
  Pull_Resistor pull_resistor_13 (.node(pull_resistor_13_node));
  Pull_Resistor pull_resistor_14 (.node(pull_resistor_14_node));
  LED led_26 (.in(pull_resistor_15_node));
  LED led_27 (.in(pull_resistor_16_node));
  LED led_28 (.in(pull_resistor_16_node));
  Pull_Resistor pull_resistor_15 (.node(pull_resistor_15_node));
  Pull_Resistor pull_resistor_16 (.node(pull_resistor_16_node));

  // Notes on the sheet:
  //   BUS
endmodule

module CLK (
  input  CLOCK_IN,
  input  HALT,
  output CLOCK_OUT
);

  wire not_1_out;

  not not_1 (not_1_out, HALT);
  and and_1 (CLOCK_OUT, CLOCK_IN, not_1_out);
endmodule
